// Logisim project projeto3.circ.circ as structural Verilog: 6 circuits, main circuit main
module main (
);

  wire clock_1_out, Reset_out;
  wire [7:0] pc_1_pc_out;
  wire [15:0] alu_1_alu_out, bancoregistros_1_rd_1_data, bancoregistros_1_rd_data,
       bancoregistros_1_rs1_1_data, bancoregistros_1_rs1_data, bancoregistros_1_rs2_1_data,
       bancoregistros_1_rs2_data, bit_extender_1_out, dot_1_out_5, dota_1_out_6, multiplexer_1_out,
       multiplexer_2_out, multiplexer_3_out, rom_1_data;

  ROM #(.dataWidth(16)) rom_1 (.addr(pc_1_pc_out), .data(rom_1_data));
  PC pc_1 (.Clock(clock_1_out), .Reset(Reset_out), .PC_out(pc_1_pc_out));
  Button Reset (.out(Reset_out));
  Clock clock_1 (.out(clock_1_out));
  assign bit_extender_1_out = {{6{rom_1_data[9]}}, rom_1_data[9:0]};  // Bit_Extender bit_extender_1
  BancoRegistros bancoregistros_1 (
    .RS1(rom_1_data[9:7]), .RS2(rom_1_data[6:4]), .OP_Res(multiplexer_1_out), .Clock(clock_1_out),
    .RD(rom_1_data[12:10]), .Reset(Reset_out), .RD_data(bancoregistros_1_rd_data),
    .RD_1_data(bancoregistros_1_rd_1_data), .RS1_data(bancoregistros_1_rs1_data),
    .RS1_1_data(bancoregistros_1_rs1_1_data), .RS2_data(bancoregistros_1_rs2_data),
    .RS2_1_data(bancoregistros_1_rs2_1_data));
  Multiplexer #(.select(3), .width(16)) multiplexer_1 (
    .in0(alu_1_alu_out), .in4(alu_1_alu_out), .in5(dot_1_out_5), .in6(dota_1_out_6), .out(multiplexer_1_out),
    .sel(rom_1_data[15:13]));  // open: in1, in2, in3, in7
  Multiplexer #(.width(16)) multiplexer_2 (
    .in0({16{1'b0}}), .in1(bancoregistros_1_rd_data), .out(multiplexer_2_out), .sel(rom_1_data[15]));
  Multiplexer #(.width(16)) multiplexer_3 (
    .in0(bit_extender_1_out), .in1(bancoregistros_1_rs1_data), .out(multiplexer_3_out), .sel(rom_1_data[15]));
  ALU alu_1 (.A(multiplexer_2_out), .B(multiplexer_3_out), .ALU_Out(alu_1_alu_out));
  DotA dota_1 (
    .RS1(bancoregistros_1_rs1_data), .RS2(bancoregistros_1_rs2_data), .RS1_1(bancoregistros_1_rs1_1_data),
    .RS2_1(bancoregistros_1_rs2_1_data), .RD(bancoregistros_1_rd_data), .out_6(dota_1_out_6));
  Dot dot_1 (
    .RD(bancoregistros_1_rd_data), .RS1(bancoregistros_1_rs1_data), .RD_1(bancoregistros_1_rd_1_data),
    .RS1_1(bancoregistros_1_rs1_1_data), .out_5(dot_1_out_5));

  // Notes on the sheet:
  //   contents of rom_1 (hex, n*v repeats v):
  //   2 403 804 c02 1001 1405 1802 1c02 8c80 a100 c260
endmodule

module PC (
  input  Clock,
  input  Reset,
  output [7:0] PC_out
);

  wire [7:0] adder_1_out;

  Adder adder_1 (.a(PC_out), .b(8'h1), .out(adder_1_out));  // open: cin, cout
  Register register_1 (.D(adder_1_out), .clk(Clock), .Q(PC_out), .clr(Reset));  // open: en
endmodule

module ALU (
  input  [15:0] A,
  input  [15:0] B,
  output [15:0] ALU_Out
);

  Adder #(.width(16)) adder_1 (.a(A), .b(B), .out(ALU_Out));  // open: cin, cout
endmodule

module BancoRegistros (
  input  [2:0] RS1,
  input  [2:0] RS2,
  input  [15:0] OP_Res,
  input  Clock,
  input  [2:0] RD,
  input  Reset,
  output [15:0] RD_data,
  output [15:0] RD_1_data,
  output [15:0] RS1_data,
  output [15:0] RS1_1_data,
  output [15:0] RS2_data,
  output [15:0] RS2_1_data
);

  wire decoder_1_out0, decoder_1_out1, decoder_1_out2, decoder_1_out3, decoder_1_out4, decoder_1_out5,
       decoder_1_out6, decoder_1_out7;
  wire [2:0] adder_1_out, adder_2_out, adder_3_out;
  wire [15:0] R0_q, R1_q, R2_q, R3_q, R4_q, R5_q, R6_q, R7_q;

  Decoder #(.select(3)) decoder_1 (
    .out0(decoder_1_out0), .out1(decoder_1_out1), .out2(decoder_1_out2), .out3(decoder_1_out3),
    .out4(decoder_1_out4), .out5(decoder_1_out5), .out6(decoder_1_out6), .out7(decoder_1_out7), .sel(RD));  // open: en
  Register #(.width(16)) R0 (.D(OP_Res), .en(decoder_1_out0), .clk(Clock), .Q(R0_q), .clr(Reset));
  Multiplexer #(.select(3), .width(16)) multiplexer_1 (
    .in0(R0_q), .in1(R1_q), .in2(R2_q), .in3(R3_q), .in4(R4_q), .in5(R5_q), .in6(R6_q), .in7(R7_q),
    .out(RD_data), .sel(RD));
  Register #(.width(16)) R1 (.D(OP_Res), .en(decoder_1_out1), .clk(Clock), .Q(R1_q), .clr(Reset));
  Adder #(.width(3)) adder_1 (.a(RD), .b(3'b001), .out(adder_1_out));  // open: cin, cout
  Register #(.width(16)) R2 (.D(OP_Res), .en(decoder_1_out2), .clk(Clock), .Q(R2_q), .clr(Reset));
  Multiplexer #(.select(3), .width(16)) multiplexer_2 (
    .in0(R0_q), .in1(R1_q), .in2(R2_q), .in3(R3_q), .in4(R4_q), .in5(R5_q), .in6(R6_q), .in7(R7_q),
    .out(RD_1_data), .sel(adder_1_out));
  Register #(.width(16)) R3 (.D(OP_Res), .en(decoder_1_out3), .clk(Clock), .Q(R3_q), .clr(Reset));
  Register #(.width(16)) R4 (.D(OP_Res), .en(decoder_1_out4), .clk(Clock), .Q(R4_q), .clr(Reset));
  Register #(.width(16)) R5 (.D(OP_Res), .en(decoder_1_out5), .clk(Clock), .Q(R5_q), .clr(Reset));
  Multiplexer #(.select(3), .width(16)) multiplexer_3 (
    .in0(R0_q), .in1(R1_q), .in2(R2_q), .in3(R3_q), .in4(R4_q), .in5(R5_q), .in6(R6_q), .in7(R7_q),
    .out(RS1_data), .sel(RS1));
  Register #(.width(16)) R6 (.D(OP_Res), .en(decoder_1_out6), .clk(Clock), .Q(R6_q), .clr(Reset));
  Adder #(.width(3)) adder_2 (.a(RS1), .b(3'b001), .out(adder_2_out));  // open: cin, cout
  Register #(.width(16)) R7 (.D(OP_Res), .en(decoder_1_out7), .clk(Clock), .Q(R7_q), .clr(Reset));
  Multiplexer #(.select(3), .width(16)) multiplexer_4 (
    .in0(R0_q), .in1(R1_q), .in2(R2_q), .in3(R3_q), .in4(R4_q), .in5(R5_q), .in6(R6_q), .in7(R7_q),
    .out(RS1_1_data), .sel(adder_2_out));
  Multiplexer #(.select(3), .width(16)) multiplexer_5 (
    .in0(R0_q), .in1(R1_q), .in2(R2_q), .in3(R3_q), .in4(R4_q), .in5(R5_q), .in6(R6_q), .in7(R7_q),
    .out(RS2_data), .sel(RS2));
  Adder #(.width(3)) adder_3 (.a(RS2), .b(3'b001), .out(adder_3_out));  // open: cin, cout
  Multiplexer #(.select(3), .width(16)) multiplexer_6 (
    .in0(R0_q), .in1(R1_q), .in2(R2_q), .in3(R3_q), .in4(R4_q), .in5(R5_q), .in6(R6_q), .in7(R7_q),
    .out(RS2_1_data), .sel(adder_3_out));
endmodule

module Dot (
  input  [15:0] RD,
  input  [15:0] RS1,
  input  [15:0] RD_1,
  input  [15:0] RS1_1,
  output [15:0] out_5
);

  wire [15:0] multiplier_1_out, multiplier_2_out;

  Multiplier #(.width(16)) multiplier_1 (.a(RD), .b(RS1), .out(multiplier_1_out));  // open: cin, cout
  Multiplier #(.width(16)) multiplier_2 (.a(RD_1), .b(RS1_1), .out(multiplier_2_out));  // open: cin, cout
  Adder #(.width(16)) adder_1 (.a(multiplier_1_out), .b(multiplier_2_out), .out(out_5));  // open: cin, cout
endmodule

module DotA (
  input  [15:0] RS1,
  input  [15:0] RS2,
  input  [15:0] RS1_1,
  input  [15:0] RS2_1,
  input  [15:0] RD,
  output [15:0] out_6
);

  wire [15:0] adder_1_out, multiplier_1_out, multiplier_2_out;

  Multiplier #(.width(16)) multiplier_1 (.a(RS1), .b(RS2), .out(multiplier_1_out));  // open: cin, cout
  Multiplier #(.width(16)) multiplier_2 (.a(RS1_1), .b(RS2_1), .out(multiplier_2_out));  // open: cin, cout
  Adder #(.width(16)) adder_1 (.a(multiplier_1_out), .b(multiplier_2_out), .out(adder_1_out));  // open: cin, cout
  Adder #(.width(16)) adder_2 (.a(adder_1_out), .b(RD), .out(out_6));  // open: cin, cout
endmodule
